// Logisim project trabalho_final_aoc1.circ as structural Verilog: 1 circuit, main circuit main
module main (
  input  A3,
  input  A2,
  input  A1,
  input  A0,
  input  B3,
  input  B2,
  input  B1,
  input  B0,
  input  A_INV,
  input  minus_B,
  input  in_11,
  input  [1:0] in_12,
  output SLT_true,
  output R3,
  output R2,
  output R1,
  output R0,
  output ZERO
);

  wire adder_1_cout, adder_1_out, adder_2_cout, adder_2_out, adder_3_cout, adder_3_out, adder_4_cout,
       adder_4_out, and_1_out, and_2_out, and_3_out, and_4_out, and_5_out, and_6_out, and_8_out, and_9_out,
       and_10_out, demultiplexer_1_out0, demultiplexer_1_out1, demultiplexer_1_out2, demultiplexer_1_out3,
       multiplexer_1_out, multiplexer_2_out, multiplexer_3_out, multiplexer_4_out, multiplexer_5_out,
       multiplexer_6_out, multiplexer_7_out, multiplexer_8_out, multiplexer_9_out, not_1_out, not_2_out,
       not_3_out, not_4_out, not_5_out, not_6_out, not_7_out, not_8_out, not_9_out, or_1_out, or_2_out,
       or_3_out, or_4_out, or_5_out, xor_1_out;

  not not_1 (not_1_out, A0);
  not not_2 (not_2_out, B0);
  not not_3 (not_3_out, A1);
  not not_4 (not_4_out, B1);
  not not_5 (not_5_out, A2);
  not not_6 (not_6_out, B2);
  not not_7 (not_7_out, A3);
  not not_8 (not_8_out, B3);
  Multiplexer #(.enable("false")) multiplexer_1 (.in0(A0), .in1(not_1_out), .out(multiplexer_1_out), .sel(and_1_out));
  Multiplexer #(.enable("false")) multiplexer_2 (.in0(A1), .in1(not_3_out), .out(multiplexer_2_out), .sel(and_1_out));
  Multiplexer #(.enable("false")) multiplexer_3 (.in0(A2), .in1(not_5_out), .out(multiplexer_3_out), .sel(and_1_out));
  Multiplexer #(.enable("false")) multiplexer_4 (.in0(A3), .in1(not_7_out), .out(multiplexer_4_out), .sel(and_1_out));
  and and_1 (and_1_out, A_INV, ~and_8_out);  // AND_Gate
  Multiplexer #(.enable("false")) multiplexer_5 (.in0(B0), .in1(not_2_out), .out(multiplexer_5_out), .sel(or_1_out));
  Multiplexer #(.enable("false")) multiplexer_6 (.in0(B1), .in1(not_4_out), .out(multiplexer_6_out), .sel(or_1_out));
  Multiplexer #(.enable("false")) multiplexer_7 (.in0(B2), .in1(not_6_out), .out(multiplexer_7_out), .sel(or_1_out));
  Multiplexer #(.enable("false")) multiplexer_8 (.in0(B3), .in1(not_8_out), .out(multiplexer_8_out), .sel(or_1_out));
  or or_1 (or_1_out, minus_B, demultiplexer_1_out3);
  and and_2 (and_2_out, multiplexer_1_out, multiplexer_5_out);
  or or_2 (or_2_out, multiplexer_1_out, multiplexer_5_out);
  Adder #(.width(1)) adder_1 (
    .a(multiplexer_1_out), .b(multiplexer_5_out), .out(adder_1_out), .cin(or_1_out), .cout(adder_1_cout));
  and and_3 (and_3_out, multiplexer_2_out, multiplexer_6_out);
  or or_3 (or_3_out, multiplexer_2_out, multiplexer_6_out);
  Adder #(.width(1)) adder_2 (
    .a(multiplexer_2_out), .b(multiplexer_6_out), .out(adder_2_out), .cin(adder_1_cout), .cout(adder_2_cout));
  and and_4 (and_4_out, multiplexer_3_out, multiplexer_7_out);
  or or_4 (or_4_out, multiplexer_3_out, multiplexer_7_out);
  Adder #(.width(1)) adder_3 (
    .a(multiplexer_3_out), .b(multiplexer_7_out), .out(adder_3_out), .cin(adder_2_cout), .cout(adder_3_cout));
  and and_5 (and_5_out, multiplexer_4_out, multiplexer_8_out);
  or or_5 (or_5_out, multiplexer_4_out, multiplexer_8_out);
  Adder #(.width(1)) adder_4 (
    .a(multiplexer_4_out), .b(multiplexer_8_out), .out(adder_4_out), .cin(adder_3_cout), .cout(adder_4_cout));
  Multiplexer #(.select(2), .enable("false")) multiplexer_9 (
    .in0(and_2_out), .in1(or_2_out), .in2(adder_1_out), .in3(adder_4_out), .out(multiplexer_9_out),
    .sel(in_12));
  Multiplexer #(.select(2), .enable("false")) multiplexer_10 (
    .in0(and_3_out), .in1(or_3_out), .in2(adder_2_out), .in3(in_11), .out(R1), .sel(in_12));
  Multiplexer #(.select(2), .enable("false")) multiplexer_11 (
    .in0(and_4_out), .in1(or_4_out), .in2(adder_3_out), .in3(in_11), .out(R2), .sel(in_12));
  Multiplexer #(.select(2), .enable("false")) multiplexer_12 (
    .in0(and_5_out), .in1(or_5_out), .in2(adder_4_out), .in3(in_11), .out(R3), .sel(in_12));
  Demultiplexer #(.select(2), .enable("false")) demultiplexer_1 (
    .out0(demultiplexer_1_out0), .out1(demultiplexer_1_out1), .out2(demultiplexer_1_out2),
    .out3(demultiplexer_1_out3), .in(1'b1), .sel(in_12));
  xor xor_1 (xor_1_out, adder_3_cout, adder_4_cout);
  LED ADD (.in(demultiplexer_1_out2));
  LED SLT (.in(demultiplexer_1_out3));
  xor xor_2 (SLT_true, xor_1_out, adder_4_out);
  and and_6 (and_6_out, SLT_true, demultiplexer_1_out3);
  LED OR_6 (.in(demultiplexer_1_out1));
  LED AND_7 (.in(demultiplexer_1_out0));
  and and_8 (and_8_out, ~demultiplexer_1_out0, ~demultiplexer_1_out1);  // AND_Gate
  and and_9 (and_9_out, and_8_out, xor_1_out);
  LED OF (.in(and_9_out));
  not not_9 (not_9_out, demultiplexer_1_out3);
  nor nor_1 (ZERO, R3, R2, R1, multiplexer_9_out);
  and and_10 (and_10_out, multiplexer_9_out, not_9_out);
  or or_7 (R0, and_10_out, and_6_out);
endmodule
