// Logisim project and e or.circ as structural Verilog: 1 circuit, main circuit main
module main (
  input  B3,
  input  B2,
  input  B1,
  input  B0,
  input  A3,
  input  A2,
  input  A1,
  input  A0,
  input  Op0,
  output R3,
  output R2,
  output R1,
  output R0
);

  wire and_1_out, and_2_out, and_3_out, and_4_out, or_1_out, or_2_out, or_3_out, or_4_out;

  and and_1 (and_1_out, A0, B0);
  or or_1 (or_1_out, A0, B0);
  and and_2 (and_2_out, A1, B1);
  or or_2 (or_2_out, A1, B1);
  and and_3 (and_3_out, A2, B2);
  or or_3 (or_3_out, A2, B2);
  and and_4 (and_4_out, A3, B3);
  or or_4 (or_4_out, A3, B3);
  Multiplexer multiplexer_1 (.in0(and_1_out), .in1(or_1_out), .out(R0), .sel(Op0));  // open: en
  Multiplexer multiplexer_2 (.in0(and_2_out), .in1(or_2_out), .out(R1), .sel(Op0));  // open: en
  Multiplexer multiplexer_3 (.in0(and_3_out), .in1(or_3_out), .out(R2), .sel(Op0));  // open: en
  Multiplexer multiplexer_4 (.in0(and_4_out), .in1(or_4_out), .out(R3), .sel(Op0));  // open: en
endmodule
