// Logisim project and or add sub.circ as structural Verilog: 1 circuit, main circuit main
module main (
  input  A3,
  input  A2,
  input  A1,
  input  A0,
  input  B3,
  input  B2,
  input  B1,
  input  B0,
  input  minus_A,
  input  minus_B,
  input  in_11,
  input  [1:0] in_12,
  output SLT,
  output R3,
  output R2,
  output R1,
  output R0,
  output OF,
  output ZERO
);

  wire adder_1_cout, adder_1_out, adder_2_cout, adder_2_out, adder_3_cout, adder_3_out, adder_4_cout,
       adder_4_out, and_1_out, and_2_out, and_3_out, and_4_out, multiplexer_1_out, multiplexer_2_out,
       multiplexer_3_out, multiplexer_4_out, multiplexer_5_out, multiplexer_6_out, multiplexer_7_out,
       multiplexer_8_out, multiplexer_9_out, multiplexer_13_out, not_1_out, not_2_out, not_3_out, not_4_out,
       not_5_out, not_6_out, not_7_out, not_8_out, or_1_out, or_2_out, or_3_out, or_4_out;

  not not_1 (not_1_out, A0);
  not not_2 (not_2_out, B0);
  not not_3 (not_3_out, A1);
  not not_4 (not_4_out, B1);
  not not_5 (not_5_out, A2);
  not not_6 (not_6_out, B2);
  not not_7 (not_7_out, A3);
  not not_8 (not_8_out, B3);
  Multiplexer multiplexer_1 (.in0(A0), .in1(not_1_out), .out(multiplexer_1_out), .sel(minus_A));  // open: en
  Multiplexer multiplexer_2 (.in0(A1), .in1(not_3_out), .out(multiplexer_2_out), .sel(minus_A));  // open: en
  Multiplexer multiplexer_3 (.in0(A2), .in1(not_5_out), .out(multiplexer_3_out), .sel(minus_A));  // open: en
  Multiplexer multiplexer_4 (.in0(A3), .in1(not_7_out), .out(multiplexer_4_out), .sel(minus_A));  // open: en
  Multiplexer multiplexer_5 (.in0(B0), .in1(not_2_out), .out(multiplexer_5_out), .sel(minus_B));  // open: en
  Multiplexer multiplexer_6 (.in0(B1), .in1(not_4_out), .out(multiplexer_6_out), .sel(minus_B));  // open: en
  Multiplexer multiplexer_7 (.in0(B2), .in1(not_6_out), .out(multiplexer_7_out), .sel(minus_B));  // open: en
  Multiplexer multiplexer_8 (.in0(B3), .in1(not_8_out), .out(multiplexer_8_out), .sel(minus_B));  // open: en
  and and_1 (and_1_out, multiplexer_1_out, multiplexer_5_out);
  or or_1 (or_1_out, multiplexer_1_out, multiplexer_5_out);
  Adder #(.width(1)) adder_1 (
    .a(multiplexer_1_out), .b(multiplexer_5_out), .out(adder_1_out), .cin(minus_B), .cout(adder_1_cout));
  and and_2 (and_2_out, multiplexer_2_out, multiplexer_6_out);
  or or_2 (or_2_out, multiplexer_2_out, multiplexer_6_out);
  Adder #(.width(1)) adder_2 (
    .a(multiplexer_2_out), .b(multiplexer_6_out), .out(adder_2_out), .cin(adder_1_cout), .cout(adder_2_cout));
  and and_3 (and_3_out, multiplexer_3_out, multiplexer_7_out);
  or or_3 (or_3_out, multiplexer_3_out, multiplexer_7_out);
  Adder #(.width(1)) adder_3 (
    .a(multiplexer_3_out), .b(multiplexer_7_out), .out(adder_3_out), .cin(adder_2_cout), .cout(adder_3_cout));
  and and_4 (and_4_out, multiplexer_4_out, multiplexer_8_out);
  or or_4 (or_4_out, multiplexer_4_out, multiplexer_8_out);
  Adder #(.width(1)) adder_4 (
    .a(multiplexer_4_out), .b(multiplexer_8_out), .out(adder_4_out), .cin(adder_3_cout), .cout(adder_4_cout));
  Multiplexer #(.select(2)) multiplexer_9 (
    .in0(and_1_out), .in1(or_1_out), .in2(adder_1_out), .in3(adder_4_out), .out(multiplexer_9_out),
    .sel(in_12));  // open: en
  Multiplexer #(.select(2)) multiplexer_10 (
    .in0(and_2_out), .in1(or_2_out), .in2(adder_2_out), .in3(in_11), .out(R1), .sel(in_12));  // open: en
  Multiplexer #(.select(2)) multiplexer_11 (
    .in0(and_3_out), .in1(or_3_out), .in2(adder_3_out), .in3(in_11), .out(R2), .sel(in_12));  // open: en
  Multiplexer #(.select(2)) multiplexer_12 (
    .in0(and_4_out), .in1(or_4_out), .in2(adder_4_out), .in3(in_11), .out(R3), .sel(in_12));  // open: en
  xor xor_1 (OF, adder_3_cout, adder_4_cout);
  xor xor_2 (SLT, OF, adder_4_out);
  Multiplexer #(.select(2)) multiplexer_13 (
    .in3(SLT), .out(multiplexer_13_out), .sel(in_12));  // open: in0, in1, in2, en
  or or_5 (R0, multiplexer_9_out, multiplexer_13_out);
  nor nor_1 (ZERO, multiplexer_9_out, R1, R2, R3);
endmodule
