// Logisim project and or add.circ as structural Verilog: 1 circuit, main circuit main
module main (
  input  B1,
  input  B0,
  input  A1,
  input  A0,
  input  Cin0,
  input  [1:0] in_6,
  output R0,
  output R0_2,
  output Cout
);

  wire adder_1_cout, adder_1_out, adder_2_out, and_1_out, and_2_out, or_1_out, or_2_out;

  and and_1 (and_1_out, A0, B0);
  or or_1 (or_1_out, A0, B0);
  Adder #(.width(1)) adder_1 (.a(A0), .b(B0), .out(adder_1_out), .cin(Cin0), .cout(adder_1_cout));
  and and_2 (and_2_out, A1, B1);
  or or_2 (or_2_out, A1, B1);
  Adder #(.width(1)) adder_2 (.a(A1), .b(B1), .out(adder_2_out), .cin(adder_1_cout), .cout(Cout));
  Multiplexer #(.select(2)) multiplexer_1 (
    .in0(and_1_out), .in1(or_1_out), .in2(adder_1_out), .out(R0), .sel(in_6));  // open: in3, en
  Multiplexer #(.select(2)) multiplexer_2 (
    .in0(and_2_out), .in1(or_2_out), .in2(adder_2_out), .out(R0_2), .sel(in_6));  // open: in3, en
endmodule
