// Logisim project somador_completo.circ as structural Verilog: 1 circuit, main circuit main
module main (
  input  A0,
  input  B0,
  input  Cin0,
  input  Cin0_2,
  input  A0_2,
  input  B0_2,
  output S0,
  output Cout0,
  output Cout0_2,
  output Cout0_3
);

  wire and_1_out, and_2_out, and_3_out, xor_1_out;

  Adder #(.width(1)) adder_1 (.a(A0_2), .b(B0_2), .out(Cout0_2), .cin(Cin0_2), .cout(Cout0_3));
  xor xor_1 (xor_1_out, A0, B0);
  and and_1 (and_1_out, Cin0, B0);
  and and_2 (and_2_out, Cin0, A0);
  and and_3 (and_3_out, B0, A0);
  xor xor_2 (S0, xor_1_out, Cin0);
  or or_1 (Cout0, and_1_out, and_2_out, and_3_out);
endmodule
